// Logisim project control-logic.circ as structural Verilog: 1 circuit, main circuit control_logic
module control_logic (
  input  [31:0] inst,
  input  BrEq,
  input  BrLt,
  output PCSel,
  output RegWEn,
  output [2:0] ImmSel,
  output BrUn,
  output ASel,
  output BSel,
  output [3:0] ALUSel,
  output MemRW,
  output [1:0] WBSel,
  output CSRSel,
  output CSRWen,
  output [5:0] out_15,
  output [5:0] out_16
);

  wire and_1_out, and_2_out, and_3_out, and_4_out, and_5_out, and_6_out, and_7_out, and_8_out, and_9_out,
       and_10_out, and_11_out, and_12_out, and_13_out, and_14_out, and_15_out, and_16_out, and_17_out,
       and_18_out, and_19_out, and_20_out, and_21_out, and_22_out, and_23_out, and_24_out, and_25_out,
       and_26_out, and_27_out, and_28_out, and_29_out, and_30_out, and_31_out, and_32_out, and_33_out,
       and_34_out, and_35_out, and_36_out, and_37_out, and_38_out, and_39_out, and_40_out, and_41_out,
       and_42_out, and_43_out, and_44_out, and_45_out, func3_000, func3_001, func3_010, func3_011, func3_100,
       func3_101, func3_110, func3_111, func7_0b0000000, func7_0b0000001, func7_0b0100000, lb, lh, lw,
       not_1_out, not_2_out, not_3_out, opcode_0b0000011, opcode_0b0010011, opcode_0b0010111,
       opcode_0b0100011, opcode_0b0110011, opcode_0b0110111, opcode_0b1100011, opcode_0b1100111,
       opcode_0b1101111, opcode_0b1110011, or_1_out, or_2_out, or_3_out, or_5_out, or_6_out,
       priority_encoder_2_out, priority_encoder_6_out, priority_encoder_7_out, sb, sh, sw;
  wire [1:0] priority_encoder_8_out, priority_encoder_9_out;
  wire [2:0] priority_encoder_1_out;
  wire [3:0] priority_encoder_3_out, priority_encoder_4_out;
  wire [5:0] bit_extender_1_out, bit_extender_2_out, bit_extender_3_out, bit_extender_4_out,
       bit_extender_5_out, bit_extender_6_out, bit_extender_7_out, bit_extender_8_out;

  Comparator #(.mode("unsigned"), .width(7)) comparator_1 (
    .a(inst[6:0]), .b(7'b0010011), .eq(opcode_0b0010011));  // open: gt, lt
  Comparator #(.mode("unsigned"), .width(7)) comparator_2 (
    .a(inst[6:0]), .b(7'b0110011), .eq(opcode_0b0110011));  // open: gt, lt
  Comparator #(.mode("unsigned"), .width(7)) comparator_3 (
    .a(inst[6:0]), .b(7'b0100011), .eq(opcode_0b0100011));  // open: gt, lt
  Comparator #(.mode("unsigned"), .width(7)) comparator_4 (
    .a(inst[6:0]), .b(7'b1100011), .eq(opcode_0b1100011));  // open: gt, lt
  Comparator #(.mode("unsigned"), .width(7)) comparator_5 (
    .a(inst[6:0]), .b(7'b0010111), .eq(opcode_0b0010111));  // open: gt, lt
  Comparator #(.mode("unsigned"), .width(7)) comparator_6 (
    .a(inst[6:0]), .b(7'b0110111), .eq(opcode_0b0110111));  // open: gt, lt
  Comparator #(.mode("unsigned"), .width(7)) comparator_7 (
    .a(inst[6:0]), .b(7'b1101111), .eq(opcode_0b1101111));  // open: gt, lt
  Comparator #(.mode("unsigned"), .width(7)) comparator_8 (
    .a(inst[6:0]), .b(7'b1100111), .eq(opcode_0b1100111));  // open: gt, lt
  Comparator #(.mode("unsigned"), .width(7)) comparator_9 (
    .a(inst[6:0]), .b(7'b1110011), .eq(opcode_0b1110011));  // open: gt, lt
  ROM #(.addrWidth(6), .dataWidth(16)) rom_1 (
    .addr(out_15), .data({RegWEn, ImmSel, BrUn, ASel, BSel, ALUSel, MemRW, WBSel, CSRSel, CSRWen}));
  and and_1 (and_1_out, func3_000, opcode_0b1100011);
  and and_2 (and_2_out, func3_001, opcode_0b1100011);
  and and_3 (and_3_out, func3_100, opcode_0b1100011);
  and and_4 (and_4_out, func3_101, opcode_0b1100011);
  and and_5 (and_5_out, func3_110, opcode_0b1100011);
  and and_6 (and_6_out, func3_111, opcode_0b1100011);
  and and_7 (and_7_out, func3_001, opcode_0b1110011);
  and and_8 (and_8_out, func3_101, opcode_0b1110011);
  Priority_Encoder priority_encoder_1 (
    .in0(and_1_out), .in1(and_2_out), .in2(and_3_out), .in3(and_4_out), .in4(and_5_out), .in5(and_6_out),
    .out(priority_encoder_1_out));  // open: in6, in7, en_in, gs, en_out
  Priority_Encoder #(.select(1)) priority_encoder_2 (
    .in0(and_7_out), .in1(and_8_out), .out(priority_encoder_2_out));  // open: gs, en_out, en_in
  Comparator #(.mode("unsigned"), .width(7)) comparator_10 (
    .a(inst[31:25]), .b({7{1'b0}}), .eq(func7_0b0000000));  // open: gt, lt
  Comparator #(.mode("unsigned"), .width(7)) comparator_11 (
    .a(inst[31:25]), .b(7'b0000001), .eq(func7_0b0000001));  // open: gt, lt
  Comparator #(.mode("unsigned"), .width(7)) comparator_12 (
    .a(inst[31:25]), .b(7'b0100000), .eq(func7_0b0100000));  // open: gt, lt
  assign bit_extender_1_out = {{3{1'b0}}, priority_encoder_1_out};  // Bit_Extender bit_extender_1
  assign bit_extender_2_out = {{5{1'b0}}, priority_encoder_2_out};  // Bit_Extender bit_extender_2
  Comparator #(.mode("unsigned"), .width(3)) comparator_13 (
    .a(inst[14:12]), .b(3'b000), .eq(func3_000));  // open: gt, lt
  Comparator #(.mode("unsigned"), .width(3)) comparator_14 (
    .a(inst[14:12]), .b(3'b001), .eq(func3_001));  // open: gt, lt
  Comparator #(.mode("unsigned"), .width(3)) comparator_15 (
    .a(inst[14:12]), .b(3'b010), .eq(func3_010));  // open: gt, lt
  Comparator #(.mode("unsigned"), .width(3)) comparator_16 (
    .a(inst[14:12]), .b(3'b011), .eq(func3_011));  // open: gt, lt
  Comparator #(.mode("unsigned"), .width(3)) comparator_17 (
    .a(inst[14:12]), .b(3'b100), .eq(func3_100));  // open: gt, lt
  Comparator #(.mode("unsigned"), .width(3)) comparator_18 (
    .a(inst[14:12]), .b(3'b101), .eq(func3_101));  // open: gt, lt
  Comparator #(.mode("unsigned"), .width(3)) comparator_19 (
    .a(inst[14:12]), .b(3'b110), .eq(func3_110));  // open: gt, lt
  Comparator #(.mode("unsigned"), .width(3)) comparator_20 (
    .a(inst[14:12]), .b(3'b111), .eq(func3_111));  // open: gt, lt
  Adder #(.width(6)) adder_1 (.a(bit_extender_1_out), .b(6'b011010), .out(out_15));  // open: cin, cout
  Adder #(.width(6)) adder_2 (.a(bit_extender_2_out), .b(6'b100100), .out(out_15));  // open: cin, cout
  and and_9 (and_9_out, opcode_0b0010011, func3_000);
  and and_10 (and_10_out, opcode_0b0010011, func3_001);
  and and_11 (and_11_out, opcode_0b0010011, func3_010);
  and and_12 (and_12_out, opcode_0b0010011, func3_100);
  and and_13 (and_13_out, opcode_0b0010011, func3_101);
  and and_14 (and_14_out, opcode_0b0010011, func3_110);
  and and_15 (and_15_out, opcode_0b0010011, func3_111);
  and and_16 (and_16_out, opcode_0b1100011, func3_000);
  and and_17 (and_17_out, opcode_0b1100011, func3_001);
  and and_18 (and_18_out, opcode_0b1100011, func3_100);
  and and_19 (and_19_out, opcode_0b1100011, func3_101);
  and and_20 (and_20_out, opcode_0b1100011, func3_110);
  and and_21 (and_21_out, opcode_0b1100011, func3_111);
  and and_22 (and_22_out, opcode_0b1100111, func3_000);
  not not_1 (not_1_out, BrEq);
  not not_2 (not_2_out, BrLt);
  not not_3 (not_3_out, BrLt);
  and and_23 (and_23_out, and_16_out, BrEq);
  and and_24 (and_24_out, and_17_out, not_1_out);
  and and_25 (and_25_out, and_18_out, BrLt);
  and and_26 (and_26_out, and_19_out, not_2_out);
  and and_27 (and_27_out, and_20_out, BrLt);
  and and_28 (and_28_out, and_21_out, not_3_out);
  and and_29 (and_29_out, and_10_out, func7_0b0000000);
  and and_30 (and_30_out, func7_0b0000000, and_13_out);
  and and_31 (and_31_out, and_13_out, func7_0b0100000);
  or or_1 (or_1_out, and_23_out, and_24_out, and_25_out);
  or or_2 (or_2_out, and_26_out, and_27_out, and_28_out);
  and and_32 (and_32_out, func3_000, func7_0b0000000, opcode_0b0110011);
  and and_33 (and_33_out, func3_000, func7_0b0000001, opcode_0b0110011);
  and and_34 (and_34_out, func3_000, func7_0b0100000, opcode_0b0110011);
  and and_35 (and_35_out, func3_001, func7_0b0000000, opcode_0b0110011);
  and and_36 (and_36_out, func3_001, func7_0b0000001, opcode_0b0110011);
  and and_37 (and_37_out, func3_011, func7_0b0000001, opcode_0b0110011);
  and and_38 (and_38_out, func3_010, func7_0b0000000, opcode_0b0110011);
  and and_39 (and_39_out, func3_100, func7_0b0000000, opcode_0b0110011);
  and and_40 (and_40_out, func3_101, func7_0b0000000, opcode_0b0110011);
  and and_41 (and_41_out, func3_101, func7_0b0100000, opcode_0b0110011);
  and and_42 (and_42_out, func3_110, func7_0b0000000, opcode_0b0110011);
  and and_43 (and_43_out, func3_111, func7_0b0000000, opcode_0b0110011);
  or or_3 (or_3_out, and_22_out, opcode_0b1101111);
  Priority_Encoder #(.select(4)) priority_encoder_3 (
    .in0(and_9_out), .in1(and_29_out), .in2(and_11_out), .in3(and_12_out), .in4(and_30_out),
    .in5(and_31_out), .in6(and_14_out), .in7(and_15_out), .out(priority_encoder_3_out));  // open: in8, in9, in10, in11, in12, in13, in14, in15, gs, en_out, en_in
  or or_4 (PCSel, or_1_out, or_2_out, or_3_out);
  assign bit_extender_3_out = {{2{1'b0}}, priority_encoder_3_out};  // Bit_Extender bit_extender_3
  Priority_Encoder #(.select(4)) priority_encoder_4 (
    .in0(and_32_out), .in1(and_33_out), .in2(and_34_out), .in3(and_35_out), .in4(and_36_out),
    .in5(and_37_out), .in6(and_38_out), .in7(and_39_out), .in8(and_40_out), .in9(and_41_out),
    .in10(and_42_out), .in11(and_43_out), .out(priority_encoder_4_out));  // open: in12, in13, in14, in15, gs, en_out, en_in
  Adder #(.width(6)) adder_3 (.a(bit_extender_3_out), .b(6'b001111), .out(out_15));  // open: cin, cout
  assign bit_extender_4_out = {{2{1'b0}}, priority_encoder_4_out};  // Bit_Extender bit_extender_4
  Adder #(.width(6)) adder_4 (.a(bit_extender_4_out), .b({6{1'b0}}), .out(out_15));  // open: cin, cout
  and and_44 (and_44_out, opcode_0b1100111, func3_000);
  or or_5 (or_5_out, and_44_out, opcode_0b0010011);
  or or_6 (or_6_out, opcode_0b0010111, opcode_0b0110111);
  Comparator #(.mode("unsigned"), .width(7)) comparator_21 (
    .a(inst[6:0]), .b(7'b0000011), .eq(opcode_0b0000011));  // open: gt, lt
  Priority_Encoder priority_encoder_5 (
    .in1(or_5_out), .in2(opcode_0b0100011), .in3(opcode_0b1100011), .in4(or_6_out), .in5(opcode_0b1101111),
    .out(ImmSel));  // open: in0, in6, in7, en_in, gs, en_out
  and and_45 (and_45_out, opcode_0b1100111, func3_000);
  and and_46 (sb, opcode_0b0100011, func3_000);
  and and_47 (sh, opcode_0b0100011, func3_001);
  and and_48 (sw, opcode_0b0100011, func3_010);
  and and_49 (lb, opcode_0b0000011, func3_000);
  and and_50 (lh, opcode_0b0000011, func3_001);
  and and_51 (lw, opcode_0b0000011, func3_010);
  Priority_Encoder #(.select(1)) priority_encoder_6 (
    .in0(opcode_0b0010111), .in1(opcode_0b0110111), .out(priority_encoder_6_out));  // open: gs, en_out, en_in
  Priority_Encoder #(.select(1)) priority_encoder_7 (
    .in0(opcode_0b1101111), .in1(and_45_out), .out(priority_encoder_7_out));  // open: gs, en_out, en_in
  assign bit_extender_5_out = {{5{1'b0}}, priority_encoder_6_out};  // Bit_Extender bit_extender_5
  assign bit_extender_6_out = {{5{1'b0}}, priority_encoder_7_out};  // Bit_Extender bit_extender_6
  Priority_Encoder #(.select(2)) priority_encoder_8 (
    .in0(sb), .in1(sh), .in2(sw), .out(priority_encoder_8_out));  // open: in3, gs, en_out, en_in
  Priority_Encoder #(.select(2)) priority_encoder_9 (
    .in0(lb), .in1(lh), .in2(lw), .out(priority_encoder_9_out));  // open: in3, gs, en_out, en_in
  Adder #(.width(6)) adder_5 (.a(bit_extender_5_out), .b(6'b100000), .out(out_15));  // open: cin, cout
  Adder #(.width(6)) adder_6 (.a(bit_extender_6_out), .b(6'b100010), .out(out_15));  // open: cin, cout
  assign bit_extender_7_out = {{4{1'b0}}, priority_encoder_8_out};  // Bit_Extender bit_extender_7
  assign bit_extender_8_out = {{4{1'b0}}, priority_encoder_9_out};  // Bit_Extender bit_extender_8
  Adder #(.width(6)) adder_7 (.a(bit_extender_7_out), .b(6'b010111), .out(out_15));  // open: cin, cout
  Adder #(.width(6)) adder_8 (.a(bit_extender_8_out), .b(6'b001100), .out(out_15));  // open: cin, cout

  assign out_16 = out_15;

  // Other names for the same wires on the sheet: opcode[6:0] = inst[6:0]; func3[2:0] = inst[14:12];
  //   func7[6:0] = inst[31:25]; ROM_INPUT[5:0] = out_15

  // Notes on the sheet:
  //   INPUTS to your circuit
  //   Connect ROM Input here ->
  //   R type
  //   lui
  //   uj
  //   jarl
  //   csr
  //   I type, opcode = 0b0010011
  //   S type
  //   SB type
  //   auipc
  //   SB type
  //   contents of rom_1 (hex, n*v repeats v):
  //   8004 8104 8184 8024 8124 8164 8044 8084 80a4 81a4 80c4 80e4 9200 9200 9200 9204 9224 9244 9284 92a4
  //   93a4 92c4 92e4 221c 221c 221c 4*360c 3e0c 3e0c c604 c3e4 d608 9208 d 600f
  //   ROM FOR CONTROL LOGIC
  //   func7 = 0
  //   func3 = 0
  //   DON'T CHANGE THE LOCATIONS OF THE INPUTS AND OUTPUTS!
  //   OUTPUT from your circuit
  //   CLOSE
  //   WIRE
  //   TO
  //   USE
  //   ROM
  //   Jalr
  //   Reminder: Use combinational logic for PCSel
  //   I type
  //   R type
  //   I type
  //   S type
  //   SB type
  //   auipc
  //   lui
  //   uj
  //   S type sb, sh, sw
  //   I type lb, lh, lw
  //   U type
  //   Jal_Jalr
endmodule
