// Logisim project cpu.circ as structural Verilog: 1 circuit, main circuit cpu
module cpu (
  input  clk,
  input  [31:0] INSTRUCTION,
  input  [31:0] MEM_READ_DATA,
  output [31:0] MEM_WRITE_ADDRESS,
  output [31:0] PROGRAM_COUNTER,
  output [31:0] ra,
  output [31:0] sp,
  output [31:0] t0,
  output [31:0] t1,
  output [31:0] t2,
  output [31:0] s0,
  output [31:0] s1,
  output [31:0] a0,
  output [31:0] tohost,
  output [3:0] MEM_WRITE_ENABLE,
  output [31:0] MEM_WRITE_DATA,
  output [31:0] out_17,
  output [1:0] out_18,
  output [3:0] out_19,
  output [31:0] out_20
);

  wire ASel, BrEq, BrLt, BrUn, BSel, CSRSel, CSRWen, func3_000, func3_001, func3_010, func3_011, func3_100,
       func3_101, func3_110, func3_111, lb, lh, lw, MemRW, opcode_0b0000011, opcode_0b0010011,
       opcode_0b0010111, opcode_0b0100011, opcode_0b0110011, opcode_0b0110111, opcode_0b1100011,
       opcode_0b1101111, opcode_0b1110011, PCSel, RegWEn, sb, sh, sw;
  wire [2:0] control_logic_1_immsel, func3;
  wire [3:0] multiplexer_7_out, multiplexer_8_out, multiplexer_9_out, multiplexer_12_out, multiplexer_13_out;
  wire [7:0] multiplexer_10_out;
  wire [11:0] CSR_address;
  wire [15:0] multiplexer_11_out;
  wire [19:0] INST_REG;
  wire [31:0] adder_1_out, bit_extender_1_out, bit_extender_2_out, bit_extender_3_out, bit_extender_4_out,
       imm, MEM_READ_DATA2, multiplexer_1_out, multiplexer_2_out, multiplexer_3_out, multiplexer_4_out,
       multiplexer_5_out, multiplexer_15_out, PC_Plus4, PC_REG, Read_Data_1, shifter_1_out, shifter_2_out,
       shifter_3_out, shifter_4_out, Write_Data;

  Adder #(.width(32)) adder_1 (.a(PROGRAM_COUNTER), .b(32'h4), .out(adder_1_out));  // open: cin, cout
  Multiplexer #(.enable("false"), .width(32)) multiplexer_1 (
    .in0(INSTRUCTION), .in1(32'h13), .out(multiplexer_1_out), .sel(PCSel));
  Multiplexer #(.enable("false"), .width(32)) multiplexer_2 (
    .in0(adder_1_out), .in1(MEM_WRITE_ADDRESS), .out(multiplexer_2_out), .sel(PCSel));
  Register #(.width(32)) Instruction_register (
    .D(multiplexer_1_out), .clk(clk), .Q({CSR_address, INST_REG[19:15], func3, INST_REG[11:0]}));  // open: en, clr
  Register #(.width(32)) PC_register (.D(PROGRAM_COUNTER), .clk(clk), .Q(PC_REG));  // open: en, clr
  Register #(.width(32)) PC (.D(multiplexer_2_out), .clk(clk), .Q(PROGRAM_COUNTER));  // open: en, clr
  Adder #(.width(32)) adder_2 (.a(32'h4), .b(PC_REG), .out(PC_Plus4));  // open: cin, cout
  control_logic control_logic_1 (
    .CSRWen(CSRWen), .PCSel(PCSel), .RegWEn(RegWEn), .ImmSel(control_logic_1_immsel), .BrUn(BrUn),
    .ASel(ASel), .BSel(BSel), .ALUSel(out_19), .MemRW(MemRW), .WBSel(out_18), .CSRSel(CSRSel),
    .inst({CSR_address, INST_REG[19:15], func3, INST_REG[11:0]}), .BrEq(BrEq), .BrLt(BrLt));
  regfile regfile_1 (
    .rs1(INST_REG[19:15]), .rs2(CSR_address[4:0]), .rd(INST_REG[11:7]), .Write_Data(Write_Data),
    .RegWEn(RegWEn), .clk(clk), .ra(ra), .sp(sp), .t0(t0), .t1(t1), .t2(t2), .s0(s0), .s1(s1), .a0(a0),
    .Read_Data_1(Read_Data_1), .Read_Data_2(out_20));
  imm_gen imm_gen_1 (
    .inst({CSR_address, INST_REG[19:15], func3, INST_REG[11:0]}), .ImmSel(control_logic_1_immsel), .imm(imm));
  Multiplexer #(.enable("false"), .width(32)) multiplexer_3 (
    .in0(Read_Data_1), .in1(imm), .out(multiplexer_3_out), .sel(CSRSel));
  branch_comp branch_comp_1 (.rs1(Read_Data_1), .rs2(out_20), .BrUn(BrUn), .BrEq(BrEq), .BrLt(BrLt));
  Multiplexer #(.enable("false"), .width(32)) multiplexer_4 (
    .in0(Read_Data_1), .in1(PC_REG), .out(multiplexer_4_out), .sel(ASel));
  Multiplexer #(.enable("false"), .width(32)) multiplexer_5 (
    .in0(out_20), .in1(imm), .out(multiplexer_5_out), .sel(BSel));
  Comparator #(.mode("unsigned"), .width(7)) comparator_1 (
    .a(INST_REG[6:0]), .b(7'b0000011), .eq(opcode_0b0000011));  // open: gt, lt
  Comparator #(.mode("unsigned"), .width(7)) comparator_2 (
    .a(INST_REG[6:0]), .b(7'b0010011), .eq(opcode_0b0010011));  // open: gt, lt
  Comparator #(.mode("unsigned"), .width(7)) comparator_3 (
    .a(INST_REG[6:0]), .b(7'b0110011), .eq(opcode_0b0110011));  // open: gt, lt
  Comparator #(.mode("unsigned"), .width(7)) comparator_4 (
    .a(INST_REG[6:0]), .b(7'b0100011), .eq(opcode_0b0100011));  // open: gt, lt
  Comparator #(.mode("unsigned"), .width(7)) comparator_5 (
    .a(INST_REG[6:0]), .b(7'b1100011), .eq(opcode_0b1100011));  // open: gt, lt
  Comparator #(.mode("unsigned"), .width(7)) comparator_6 (
    .a(INST_REG[6:0]), .b(7'b0010111), .eq(opcode_0b0010111));  // open: gt, lt
  Comparator #(.mode("unsigned"), .width(7)) comparator_7 (
    .a(INST_REG[6:0]), .b(7'b0110111), .eq(opcode_0b0110111));  // open: gt, lt
  Comparator #(.mode("unsigned"), .width(7)) comparator_8 (
    .a(INST_REG[6:0]), .b(7'b1101111), .eq(opcode_0b1101111));  // open: gt, lt
  Comparator #(.mode("unsigned"), .width(7)) comparator_9 (
    .a(INST_REG[6:0]), .b(7'b1110011), .eq(opcode_0b1110011));  // open: gt, lt
  alu alu_1 (.Result(MEM_WRITE_ADDRESS), .A(multiplexer_4_out), .B(multiplexer_5_out), .ALUSel(out_19));
  csr csr_1 (.CSR_address(CSR_address), .CSR_din(multiplexer_3_out), .CSR_WE(CSRWen), .clk(clk), .tohost(tohost));
  Comparator #(.mode("unsigned"), .width(3)) comparator_10 (.a(func3), .b(3'b000), .eq(func3_000));  // open: gt, lt
  Comparator #(.mode("unsigned"), .width(3)) comparator_11 (.a(func3), .b(3'b001), .eq(func3_001));  // open: gt, lt
  Comparator #(.mode("unsigned"), .width(3)) comparator_12 (.a(func3), .b(3'b010), .eq(func3_010));  // open: gt, lt
  Comparator #(.mode("unsigned"), .width(3)) comparator_13 (.a(func3), .b(3'b011), .eq(func3_011));  // open: gt, lt
  Comparator #(.mode("unsigned"), .width(3)) comparator_14 (.a(func3), .b(3'b100), .eq(func3_100));  // open: gt, lt
  Comparator #(.mode("unsigned"), .width(3)) comparator_15 (.a(func3), .b(3'b101), .eq(func3_101));  // open: gt, lt
  Comparator #(.mode("unsigned"), .width(3)) comparator_16 (.a(func3), .b(3'b110), .eq(func3_110));  // open: gt, lt
  Comparator #(.mode("unsigned"), .width(3)) comparator_17 (.a(func3), .b(3'b111), .eq(func3_111));  // open: gt, lt
  Multiplexer #(.enable("false"), .select(2), .width(32)) multiplexer_6 (
    .in0(MEM_READ_DATA2), .in1(MEM_WRITE_ADDRESS), .in2(PC_Plus4), .out(Write_Data), .sel(out_18));  // open: in3
  Multiplexer #(.enable("false"), .width(4)) multiplexer_7 (
    .in0(4'b0000), .in1(multiplexer_8_out), .out(multiplexer_7_out), .sel(sb));
  Multiplexer #(.enable("false"), .select(2), .width(4)) multiplexer_8 (
    .in0(4'b0001), .in1(4'b0010), .in2(4'b0100), .in3(4'b1000), .out(multiplexer_8_out),
    .sel(MEM_WRITE_ADDRESS[1:0]));
  Multiplexer #(.enable("false"), .select(2), .width(4)) multiplexer_9 (
    .in0(4'b0011), .in2(4'b1100), .out(multiplexer_9_out), .sel(MEM_WRITE_ADDRESS[1:0]));  // open: in1, in3
  Multiplexer #(.enable("false"), .select(2), .width(8)) multiplexer_10 (
    .in0(MEM_READ_DATA[7:0]), .in1(MEM_READ_DATA[15:8]), .in2(MEM_READ_DATA[23:16]),
    .in3(MEM_READ_DATA[31:24]), .out(multiplexer_10_out), .sel(MEM_WRITE_ADDRESS[1:0]));
  Multiplexer #(.enable("false"), .select(2), .width(16)) multiplexer_11 (
    .in0(MEM_READ_DATA[15:0]), .in2(MEM_READ_DATA[31:16]), .out(multiplexer_11_out),
    .sel(MEM_WRITE_ADDRESS[1:0]));  // open: in1, in3
  Multiplexer #(.enable("false"), .width(4)) multiplexer_12 (
    .in0(multiplexer_7_out), .in1(multiplexer_9_out), .out(multiplexer_12_out), .sel(sh));
  assign bit_extender_1_out = {{16{1'b0}}, out_20[15:0]};  // Bit_Extender bit_extender_1
  and and_1 (sb, opcode_0b0100011, func3_000);
  and and_2 (sh, opcode_0b0100011, func3_001);
  and and_3 (sw, opcode_0b0100011, func3_010);
  Multiplexer #(.enable("false"), .width(4)) multiplexer_13 (
    .in0(multiplexer_12_out), .in1(4'b1111), .out(multiplexer_13_out), .sel(sw));
  assign bit_extender_2_out = {{24{1'b0}}, out_20[7:0]};  // Bit_Extender bit_extender_2
  Shifter #(.width(32)) shifter_1 (.in(bit_extender_1_out), .\dist (5'b10000), .out(shifter_1_out));
  and and_4 (lb, opcode_0b0000011, func3_000);
  and and_5 (lh, opcode_0b0000011, func3_001);
  and and_6 (lw, opcode_0b0000011, func3_010);
  assign bit_extender_3_out = {{24{multiplexer_10_out[7]}}, multiplexer_10_out};  // Bit_Extender bit_extender_3
  assign bit_extender_4_out = {{16{multiplexer_11_out[15]}}, multiplexer_11_out};  // Bit_Extender bit_extender_4
  Shifter #(.width(32)) shifter_2 (.in(bit_extender_2_out), .\dist (5'b01000), .out(shifter_2_out));
  Shifter #(.width(32)) shifter_3 (.in(bit_extender_2_out), .\dist (5'b10000), .out(shifter_3_out));
  Shifter #(.width(32)) shifter_4 (.in(bit_extender_2_out), .\dist (5'b11000), .out(shifter_4_out));
  Multiplexer #(.enable("false"), .width(32)) multiplexer_14 (
    .in0(multiplexer_15_out), .in1(bit_extender_3_out), .out(MEM_READ_DATA2), .sel(lb));
  Multiplexer #(.enable("false"), .width(32)) multiplexer_15 (
    .in0(MEM_READ_DATA), .in1(bit_extender_4_out), .out(multiplexer_15_out), .sel(lh));
  Multiplexer #(.enable("false"), .width(4)) multiplexer_16 (
    .in0(4'b0000), .in1(multiplexer_13_out), .out(MEM_WRITE_ENABLE), .sel(MemRW));
  Multiplexer #(.enable("false"), .select(4), .width(32)) multiplexer_17 (
    .in0(MEM_READ_DATA), .in1(bit_extender_2_out), .in2(shifter_2_out), .in3(bit_extender_1_out),
    .in4(shifter_3_out), .in8(shifter_4_out), .in12(shifter_1_out), .in15(out_20), .out(MEM_WRITE_DATA),
    .sel(MEM_WRITE_ENABLE));  // open: in5, in6, in7, in9, in10, in11, in13, in14

  assign out_17 = MEM_WRITE_ADDRESS;

  // Other names for the same wires on the sheet: ALU_DATA[31:0] = MEM_WRITE_ADDRESS;
  //   LAST_2_BITS[1:0] = MEM_WRITE_ADDRESS[1:0]; opcode[6:0] = INST_REG[6:0]; rd[4:0] = INST_REG[11:7];
  //   INST_REG (some bits) = {CSR_address, func3}; rs1[4:0] = INST_REG[19:15]; rs2[4:0] = CSR_address[4:0];
  //   func7[6:0] = CSR_address[11:5]; Read_Data_2[31:0] = out_20; WBSel[1:0] = out_18

  // Notes on the sheet:
  //   Output to IMEM
  //   IMEM (do **NOT** move this)
  //   Inputs from IMEM
  //   It is OK to move the PC, RegFile, ALU, MEM, Branch Comp, Imm Gen, and Control Logic to wherever is most convenient for you when constructing your CPU, and to delete this text
  //   Inputs/Outputs for testing. Do **NOT** move these.
  //   R type
  //   S type
  //   SB type
  //   auipc
  //   lui
  //   uj
  //   ALU
  //   I type, opcode = 0b0010011
  //   func3 = 0
  //   Outputs To DMEM
  //   DMEM (do **NOT** move this)
  //   Inputs From DMEM
  //   I type lb, lh, lw
endmodule
