// Logisim project csr-harness.circ as structural Verilog: 1 circuit, main circuit csr_harness
module csr_harness (
  input  [31:0] INSTRUCTION,
  input  clk,
  output [31:0] PROGRAM_COUNTER,
  output [31:0] ra,
  output [31:0] sp,
  output [31:0] t0,
  output [31:0] t1,
  output [31:0] t2,
  output [31:0] s0,
  output [31:0] s1,
  output [31:0] a0,
  output [31:0] tohost
);

  wire [3:0] cpu_1_mem_write_enable;
  wire [31:0] cpu_1_mem_write_address, cpu_1_mem_write_data, mem_1_read_data;

  cpu cpu_1 (
    .clk(clk), .INSTRUCTION(INSTRUCTION), .MEM_READ_DATA(mem_1_read_data),
    .MEM_WRITE_ADDRESS(cpu_1_mem_write_address), .PROGRAM_COUNTER(PROGRAM_COUNTER), .ra(ra), .sp(sp),
    .t0(t0), .t1(t1), .t2(t2), .s0(s0), .s1(s1), .a0(a0), .tohost(tohost),
    .MEM_WRITE_ENABLE(cpu_1_mem_write_enable), .MEM_WRITE_DATA(cpu_1_mem_write_data));
  mem mem_1 (
    .Address(cpu_1_mem_write_address), .Write_En(cpu_1_mem_write_enable), .Write_Data(cpu_1_mem_write_data),
    .clk(clk), .Read_Data(mem_1_read_data));

  // Notes on the sheet:
  //   YOUR CPU SHOULD FIT IN HERE!
endmodule
