// Logisim project cpu-edge-all-regs.circ as structural Verilog: 1 circuit, main circuit run_main
module run_main (
  output [31:0] ra,
  output [31:0] sp,
  output [31:0] t0,
  output [31:0] t1,
  output [31:0] t2,
  output [31:0] s0,
  output [31:0] s1,
  output [31:0] a0,
  output [31:0] Requested_Address,
  output [31:0] Requested_Instruction,
  output [15:0] Time_Step,
  output halt
);

  wire clk;

  Clock clock_1 (.out(clk));
  // Probe on Requested_Address
  cpu_harness cpu_harness_1 (
    .INSTRUCTION(Requested_Instruction), .clk(clk), .PROGRAM_COUNTER(Requested_Address), .ra(ra), .sp(sp),
    .t0(t0), .t1(t1), .t2(t2), .s0(s0), .s1(s1), .a0(a0));
  ROM #(.addrWidth(14), .dataWidth(32)) rom_1 (.addr(Requested_Address[15:2]), .data(Requested_Instruction));
  // Probe on Requested_Instruction
  Counter #(.max('hffff), .width(16)) counter_1 (.clk(clk), .Q(Time_Step));  // open: clr, load, up, count, D, carry
  Comparator #(.width(16)) comparator_1 (.a(Time_Step), .b(16'h42), .eq(halt));  // open: gt, lt

  // Other names for the same wires on the sheet: INSTRUCTION[31:0] = Requested_Instruction;
  //   PROGRAM_COUNTER[31:0] = Requested_Address

  // Notes on the sheet:
  //   contents of rom_1 (hex, n*v repeats v):
  //   13 413 100093 8413 200113 10413 300193 18413 400213 20413 500293 28413 600313 30413 700393 38413
  //   800413 40413 900493 48413 A00513 50413 B00593 58413 C00613 60413 D00693 68413 E00713 70413 F00793
  //   78413 1000813 80413 1100893 88413 1200913 90413 1300993 98413 1400A13 A0413 1500A93 A8413 1600B13
  //   B0413 1700B93 B8413 1800C13 C0413 1900C93 C8413 1A00D13 D0413 1B00D93 D8413 1C00E13 E0413 1D00E93
  //   E8413 1E00F13 F0413 1F00F93 F8413
  //   Instruction Memory
  //   Halts Execution After Constant # of Clock Cycles
  //   Constant
endmodule
