// Logisim project cpu-edge-jump-far.circ as structural Verilog: 1 circuit, main circuit run_main
module run_main (
  output [31:0] ra,
  output [31:0] sp,
  output [31:0] t0,
  output [31:0] t1,
  output [31:0] t2,
  output [31:0] s0,
  output [31:0] s1,
  output [31:0] a0,
  output [31:0] Requested_Address,
  output [31:0] Requested_Instruction,
  output [15:0] Time_Step,
  output halt
);

  wire clk;

  Clock clock_1 (.out(clk));
  // Probe on Requested_Address
  cpu_harness cpu_harness_1 (
    .INSTRUCTION(Requested_Instruction), .clk(clk), .PROGRAM_COUNTER(Requested_Address), .ra(ra), .sp(sp),
    .t0(t0), .t1(t1), .t2(t2), .s0(s0), .s1(s1), .a0(a0));
  ROM #(.addrWidth(14), .dataWidth(32)) rom_1 (.addr(Requested_Address[15:2]), .data(Requested_Instruction));
  // Probe on Requested_Instruction
  Counter #(.max('hffff), .width(16)) counter_1 (.clk(clk), .Q(Time_Step));  // open: clr, load, up, count, D, carry
  Comparator #(.width(16)) comparator_1 (.a(Time_Step), .b(16'h7), .eq(halt));  // open: gt, lt

  // Other names for the same wires on the sheet: INSTRUCTION[31:0] = Requested_Instruction;
  //   PROGRAM_COUNTER[31:0] = Requested_Address

  // Notes on the sheet:
  //   contents of rom_1 (hex, n*v repeats v):
  //   40B7 FF808093 8067 100413 200413 300413 400413 500413 600413 700413 800413 900413 A00413 B00413
  //   C00413 D00413 E00413 F00413 1000413 1100413 1200413 1300413 1400413 1500413 1600413 1700413 1800413
  //   1900413 1A00413 1B00413 1C00413 1D00413 1E00413 1F00413 2000413 2100413 2200413 2300413 2400413
  //   2500413 2600413 2700413 2800413 2900413 2A00413 2B00413 2C00413 2D00413 2E00413 2F00413 3000413
  //   3100413 3200413 3300413 3400413 3500413 3600413 3700413 3800413 3900413 3A00413 3B00413 3C00413
  //   3D00413 3E00413 3F00413 4000413 4100413 4200413 4300413 4400413 4500413 4600413 4700413 4800413
  //   4900413 4A00413 4B00413 4C00413 4D00413 4E00413 4F00413 5000413 5100413 5200413 5300413 5400413
  //   5500413 5600413 5700413 5800413 5900413 5A00413 5B00413 5C00413 5D00413 5E00413 5F00413 6000413
  //   6100413 6200413 6300413 6400413 6500413 6600413 6700413 6800413 6900413 6A00413 6B00413 6C00413
  //   6D00413 6E00413 6F00413 7000413 7100413 7200413 7300413 7400413 7500413 7600413 7700413 7800413
  //   7900413 7A00413 7B00413 7C00413 7D00413 7E00413 7F00413 8000413 8100413 8200413 8300413 8400413
  //   8500413 8600413 8700413 8800413 8900413 8A00413 8B00413 8C00413 8D00413 8E00413 8F00413 9000413
  //   9100413 9200413 9300413 9400413 9500413 9600413 9700413 9800413 9900413 9A00413 9B00413 9C00413
  //   9D00413 9E00413 9F00413 A000413 A100413 A200413 A300413 A400413 A500413 A600413 A700413 A800413
  //   A900413 AA00413 AB00413 AC00413 AD00413 AE00413 AF00413 B000413 B100413 B200413 B300413 B400413
  //   B500413 B600413 B700413 B800413 B900413 BA00413 BB00413 BC00413 BD00413 BE00413 BF00413 C000413
  //   C100413 C200413 C300413 C400413 C500413 C600413 C700413 C800413 C900413 CA00413 CB00413 CC00413
  //   CD00413 CE00413 CF00413 D000413 D100413 D200413 D300413 D400413 D500413 D600413 D700413 D800413
  //   D900413 DA00413 DB00413 DC00413 DD00413 DE00413 DF00413 E000413 E100413 E200413 E300413 E400413
  //   E500413 E600413 E700413 E800413 E900413 EA00413 EB00413 EC00413 ED00413 EE00413 EF00413 F000413
  //   F100413 F200413 F300413 F400413 F500413 F600413 F700413 F800413 F900413 FA00413 FB00413 FC00413
  //   FD00413 FE00413 FF00413 10000413 10100413 10200413 10300413 10400413 10500413 10600413 10700413
  //   10800413 10900413 10A00413 10B00413 10C00413 10D00413 10E00413 10F00413 11000413 11100413 11200413
  //   11300413 11400413 11500413 11600413 11700413 11800413 11900413 11A00413 11B00413 11C00413 11D00413
  //   11E00413 11F00413 12000413 12100413 12200413 12300413 12400413 12500413 12600413 12700413 12800413
  //   12900413 12A00413 12B00413 12C00413 12D00413 12E00413 12F00413 13000413 13100413 13200413 13300413
  //   13400413 13500413 13600413 13700413 13800413 13900413 13A00413 13B00413 13C00413 13D00413 13E00413
  //   13F00413 14000413 14100413 14200413 14300413 14400413 14500413 14600413 14700413 14800413 14900413
  //   14A00413 14B00413 14C00413 14D00413 14E00413 14F00413 15000413 15100413 15200413 15300413 15400413
  //   15500413 15600413 15700413 15800413 15900413 15A00413 15B00413 15C00413 15D00413 15E00413 15F00413
  //   16000413 16100413 16200413 16300413 16400413 16500413 16600413 16700413 16800413 16900413 16A00413
  //   16B00413 16C00413 16D00413 16E00413 16F00413 17000413 17100413 17200413 17300413 17400413 17500413
  //   17600413 17700413 17800413 17900413 17A00413 17B00413 17C00413 17D00413 17E00413 17F00413 18000413
  //   18100413 18200413 18300413 18400413 18500413 18600413 18700413 18800413 18900413 18A00413 18B00413
  //   18C00413 18D00413 18E00413 18F00413 19000413 19100413 19200413 19300413 19400413 19500413 19600413
  //   19700413 19800413 19900413 19A00413 19B00413 19C00413 19D00413 19E00413 19F00413 1A000413 1A100413
  //   1A200413 1A300413 1A400413 1A500413 1A600413 1A700413 1A800413 1A900413 1AA00413 1AB00413 1AC00413
  //   1AD00413 1AE00413 1AF00413 1B000413 1B100413 1B200413 1B300413 1B400413 1B500413 1B600413 1B700413
  //   1B800413 1B900413 1BA00413 1BB00413 1BC00413 1BD00413 1BE00413 1BF00413 1C000413 1C100413 1C200413
  //   1C300413 1C400413 1C500413 1C600413 1C700413 1C800413 1C900413 1CA00413 1CB00413 1CC00413 1CD00413
  //   1CE00413 1CF00413 1D000413 1D100413 1D200413 1D300413 1D400413 1D500413 1D600413 1D700413 1D800413
  //   1D9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
  //   Instruction Memory
  //   Halts Execution After Constant # of Clock Cycles
  //   Constant
endmodule
